// Logisim project guessthenumber.circ as structural Verilog: 20 circuits, main circuit main
// reset
module main (
  input  Confirmar,
  input  [3:0] CHUTE
);

  wire decoder7segmentos_1_a, decoder7segmentos_1_b, decoder7segmentos_1_c, decoder7segmentos_1_d,
       decoder7segmentos_1_e, decoder7segmentos_1_f, decoder7segmentos_1_g, minigame_1_out_4, random_out;

  // RGBLed #(.multibit("true")) rgbled_1: pin names not known
  minigame minigame_1 (
    .out_4(minigame_1_out_4), .in_2(CHUTE), .in_3(random_out), .confirmar(Confirmar));  // open: out_5, out_6
  Button random (.out(random_out));
  LED led_1 (.in(minigame_1_out_4));
  decoder7segmentos decoder7segmentos_1 (
    .in_1(CHUTE), .a(decoder7segmentos_1_a), .c(decoder7segmentos_1_c), .e(decoder7segmentos_1_e),
    .g(decoder7segmentos_1_g), .b(decoder7segmentos_1_b), .d(decoder7segmentos_1_d), .f(decoder7segmentos_1_f));
  _7_Segment_Display u_7_segment_display_1 (
    .g(decoder7segmentos_1_g), .f(decoder7segmentos_1_f), .a(decoder7segmentos_1_a),
    .b(decoder7segmentos_1_b), .e(decoder7segmentos_1_e), .d(decoder7segmentos_1_d), .c(decoder7segmentos_1_c));  // open: dp
endmodule

// Mini Game
module minigame (
  input  confirmar,
  input  [3:0] in_2,
  input  in_3,
  output out_4,
  output [7:0] out_5,
  output [7:0] out_6
);

  wire comparador_a___b;
  wire [3:0] \diferença_1_out_3 , numaleatorio_1_out_2;
  wire [7:0] cores_1_azul, cores_1_vermelho, ext8bits_out_2;

  assign out_5 = cores_1_vermelho & ext8bits_out_2;  // AND_Gate and_1, 8 bits wide
  cores cores_1 (.\diferença_in (\diferença_1_out_3 ), .vermelho(cores_1_vermelho), .azul(cores_1_azul));
  \diferença  \diferença_1  (.out_3(\diferença_1_out_3 ), .A(numaleatorio_1_out_2), .B(in_2));
  assign out_6 = cores_1_azul & ext8bits_out_2;  // AND_Gate and_2, 8 bits wide
  numaleatorio numaleatorio_1 (.out_2(numaleatorio_1_out_2), .in_1(in_3));
  extensorde8bits ext8bits (.in_1(confirmar), .out_2(ext8bits_out_2));
  and and_3 (out_4, confirmar, comparador_a___b);
  comparador4bits comparador (.A(numaleatorio_1_out_2), .B(in_2), .A___B(comparador_a___b));  // open: A___B_2, A___B_3
endmodule

module LED_A (
  input  E3,
  input  E2,
  input  E1,
  input  E0,
  output out_5
);

  wire and_1_out, and_2_out, and_3_out, and_4_out, and_5_out, and_6_out;

  and and_1 (and_1_out, E3, ~E0);  // AND_Gate
  and and_2 (and_2_out, ~E3, E1);  // AND_Gate
  and and_3 (and_3_out, E3, E2, E1, E0);
  and and_4 (and_4_out, E3, ~E2, ~E1, E0);  // AND_Gate
  and and_5 (and_5_out, ~E3, ~E2, ~E1, ~E0);  // AND_Gate
  and and_6 (and_6_out, ~E3, E2, ~E1, E0);  // AND_Gate
  or or_1 (out_5, and_1_out, and_2_out, and_3_out, and_4_out, and_5_out, and_6_out);
endmodule

module LED_B (
  input  E3,
  input  E2,
  input  E1,
  input  E0,
  output out_5
);

  wire and_1_out, and_2_out, and_3_out, and_4_out, and_5_out;

  and and_1 (and_1_out, ~E3, ~E2);  // AND_Gate
  and and_2 (and_2_out, E3, ~E1, E0);  // AND_Gate
  and and_3 (and_3_out, E3, ~E2, ~E0);  // AND_Gate
  and and_4 (and_4_out, ~E3, E2, ~E1, ~E0);  // AND_Gate
  and and_5 (and_5_out, ~E3, E2, E1, E0);  // AND_Gate
  or or_1 (out_5, and_1_out, and_2_out, and_3_out, and_4_out, and_5_out);
endmodule

module LED_C (
  input  E3,
  input  E2,
  input  E1,
  input  E0,
  output out_5
);

  wire and_1_out, and_2_out, and_3_out, and_4_out, and_5_out;

  and and_1 (and_1_out, ~E3, ~E1);  // AND_Gate
  and and_2 (and_2_out, E3, ~E2);  // AND_Gate
  and and_3 (and_3_out, ~E3, E1, E0);  // AND_Gate
  and and_4 (and_4_out, ~E3, E2, E1, ~E0);  // AND_Gate
  and and_5 (and_5_out, E3, E2, ~E1, E0);  // AND_Gate
  or or_1 (out_5, and_1_out, and_2_out, and_3_out, and_4_out, and_5_out);
endmodule

module LED_D (
  input  E3,
  input  E2,
  input  E1,
  input  E0,
  output out_5
);

  wire and_1_out, and_2_out, and_3_out, and_4_out, and_5_out, and_6_out;

  and and_1 (and_1_out, E3, ~E1);  // AND_Gate
  and and_2 (and_2_out, ~E2, E1, E0);  // AND_Gate
  and and_3 (and_3_out, ~E3, E1, ~E0);  // AND_Gate
  and and_4 (and_4_out, E3, E2, E1, ~E0);  // AND_Gate
  and and_5 (and_5_out, ~E3, ~E2, ~E1, ~E0);  // AND_Gate
  and and_6 (and_6_out, ~E3, E2, ~E1, E0);  // AND_Gate
  or or_1 (out_5, and_1_out, and_2_out, and_3_out, and_4_out, and_5_out, and_6_out);
endmodule

module LED_E (
  input  E3,
  input  E2,
  input  E1,
  input  E0,
  output out_5
);

  wire and_1_out, and_2_out, and_3_out, and_4_out;

  and and_1 (and_1_out, E3, E2);
  and and_2 (and_2_out, ~E2, ~E0);  // AND_Gate
  and and_3 (and_3_out, E3, ~E2, E1, E0);  // AND_Gate
  and and_4 (and_4_out, ~E3, E2, E1, ~E0);  // AND_Gate
  or or_1 (out_5, and_1_out, and_2_out, and_3_out, and_4_out);
endmodule

module LED_F (
  input  E3,
  input  E2,
  input  E1,
  input  E0,
  output out_5
);

  wire and_1_out, and_2_out, and_3_out, and_4_out, and_5_out;

  and and_1 (and_1_out, E3, E1);
  and and_2 (and_2_out, ~E1, ~E0);  // AND_Gate
  and and_3 (and_3_out, E3, ~E2, ~E1, E0);  // AND_Gate
  and and_4 (and_4_out, ~E3, E2, ~E1, E0);  // AND_Gate
  and and_5 (and_5_out, ~E3, E2, E1, ~E0);  // AND_Gate
  or or_1 (out_5, and_1_out, and_2_out, and_3_out, and_4_out, and_5_out);
endmodule

module LED_G (
  input  E3,
  input  E2,
  input  E1,
  input  E0,
  output out_5
);

  wire and_1_out, and_2_out, and_3_out, and_4_out, and_5_out, and_6_out;

  and and_1 (and_1_out, ~E2, E1);  // AND_Gate
  and and_2 (and_2_out, E3, E2, E1);
  and and_3 (and_3_out, E3, ~E2, ~E1);  // AND_Gate
  and and_4 (and_4_out, ~E3, E2, ~E0);  // AND_Gate
  and and_5 (and_5_out, E3, E2, ~E1, E0);  // AND_Gate
  and and_6 (and_6_out, ~E3, E2, ~E1, E0);  // AND_Gate
  or or_1 (out_5, and_1_out, and_2_out, and_3_out, and_4_out, and_5_out, and_6_out);
endmodule

// DECODER
module decoder7segmentos (
  input  [3:0] in_1,
  output a,
  output b,
  output c,
  output d,
  output e,
  output f,
  output g
);

  LED_A led_a_1 (.E3(in_1[3]), .E2(in_1[2]), .E1(in_1[1]), .E0(in_1[0]), .out_5(a));
  LED_B led_b_1 (.E3(in_1[3]), .E2(in_1[2]), .E1(in_1[1]), .E0(in_1[0]), .out_5(b));
  LED_C led_c_1 (.E3(in_1[3]), .E2(in_1[2]), .E1(in_1[1]), .E0(in_1[0]), .out_5(c));
  LED_E led_e_1 (.E3(in_1[3]), .E2(in_1[2]), .E1(in_1[1]), .E0(in_1[0]), .out_5(e));
  LED_G led_g_1 (.E3(in_1[3]), .E2(in_1[2]), .E1(in_1[1]), .E0(in_1[0]), .out_5(g));
  LED_D led_d_1 (.E3(in_1[3]), .E2(in_1[2]), .E1(in_1[1]), .E0(in_1[0]), .out_5(d));
  LED_F led_f_1 (.E3(in_1[3]), .E2(in_1[2]), .E1(in_1[1]), .E0(in_1[0]), .out_5(f));
endmodule

module display7seg (
  input  [3:0] in_1
);

  wire decoder7segmentos_1_p2, decoder7segmentos_1_p3, decoder7segmentos_1_p4, undriven, undriven_2;

  // decoder7segmentos decoder7segmentos_1: pin names not known; wires that end beside it: in_1, decoder7segmentos_1_p2, decoder7segmentos_1_p3, decoder7segmentos_1_p4, decoder7segmentos_1_p4
  _7_Segment_Display u_7_segment_display_1 (
    .g(decoder7segmentos_1_p4), .f(undriven), .a(decoder7segmentos_1_p2), .b(decoder7segmentos_1_p4),
    .e(decoder7segmentos_1_p4), .d(undriven_2), .c(decoder7segmentos_1_p3));  // open: dp
endmodule

// RANDOM
module numaleatorio (
  input  in_1,
  output [3:0] out_2
);

  Random #(.width(4)) random_1 (.clk(in_1), .out(out_2));  // open: next, clr
endmodule

module subtrator (
  input  [3:0] A,
  input  [3:0] B,
  output [3:0] Dif
);

  wire and_1_out, and_2_out, and_3_out, and_4_out, and_5_out, and_6_out, and_7_out, and_8_out, and_9_out,
       and_10_out, or_1_out, or_2_out;

  xor xor_1 (Dif[0], B[0], A[0]);
  and and_1 (and_1_out, B[0], ~A[0]);  // AND_Gate
  ExactlyOne xor_2 (.out(Dif[1]), .in0(and_1_out), .in1(B[1]), .in2(A[1]));
  and and_2 (and_2_out, B[1], and_1_out);
  and and_3 (and_3_out, ~A[1], and_1_out);  // AND_Gate
  and and_4 (and_4_out, ~A[1], B[1]);  // AND_Gate
  or or_1 (or_1_out, and_2_out, and_3_out, and_4_out);
  ExactlyOne xor_3 (.out(Dif[2]), .in0(or_1_out), .in1(B[2]), .in2(A[2]));
  and and_5 (and_5_out, B[2], or_1_out);
  or or_2 (or_2_out, and_5_out, and_6_out, and_7_out);
  and and_6 (and_6_out, ~A[2], or_1_out);  // AND_Gate
  and and_7 (and_7_out, ~A[2], B[2]);  // AND_Gate
  ExactlyOne xor_4 (.out(Dif[3]), .in0(or_2_out), .in1(B[3]), .in2(A[3]));
  and and_8 (and_8_out, A[3], or_2_out);
  and and_9 (and_9_out, ~A[3], or_2_out);  // AND_Gate
  and and_10 (and_10_out, ~A[3], B[3]);  // AND_Gate
  // OR_Gate or_3 has open pins: in0=and_8_out, in1=and_9_out, in2=and_10_out, out=open
endmodule

module comparador4bits (
  input  [3:0] A,
  input  [3:0] B,
  output A___B,
  output A___B_2,
  output A___B_3
);

  wire and_2_out, and_3_out, and_4_out, and_5_out, xnor_1_out, xnor_2_out, xnor_3_out, xnor_4_out,
       xnor_5_out, xnor_6_out, xnor_7_out, xnor_8_out, xnor_9_out, xnor_10_out;

  xnor xnor_1 (xnor_1_out, A[3], B[3]);
  xnor xnor_2 (xnor_2_out, A[2], B[2]);
  xnor xnor_3 (xnor_3_out, A[1], B[1]);
  xnor xnor_4 (xnor_4_out, A[0], B[0]);
  xnor xnor_5 (xnor_5_out, A[3], B[3]);
  xnor xnor_6 (xnor_6_out, A[3], B[3]);
  xnor xnor_7 (xnor_7_out, A[2], B[2]);
  xnor xnor_8 (xnor_8_out, A[3], B[3]);
  xnor xnor_9 (xnor_9_out, A[2], B[2]);
  xnor xnor_10 (xnor_10_out, A[1], B[1]);
  and and_1 (A___B, xnor_1_out, xnor_2_out, xnor_3_out, xnor_4_out);
  and and_2 (and_2_out, A[3], ~B[3]);  // AND_Gate
  and and_3 (and_3_out, xnor_5_out, A[2], ~B[2]);  // AND_Gate
  and and_4 (and_4_out, xnor_6_out, xnor_7_out, A[1], ~B[1]);  // AND_Gate
  and and_5 (and_5_out, xnor_8_out, xnor_9_out, xnor_10_out, A[0], ~B[0]);  // AND_Gate
  or or_1 (A___B_2, and_2_out, and_3_out, and_4_out, and_5_out);
  nor nor_1 (A___B_3, A___B, A___B_2);
endmodule

module multiplexador (
  input  [3:0] A,
  input  [3:0] B,
  input  S,
  output [3:0] out_4
);

  wire [3:0] and_1_out, and_2_out, extensorde4bits_1_out_2;

  extensorde4bits extensorde4bits_1 (.in_1(S), .out_2(extensorde4bits_1_out_2));
  assign and_1_out = ~extensorde4bits_1_out_2 & A;  // AND_Gate and_1, 4 bits wide
  assign and_2_out = extensorde4bits_1_out_2 & B;  // AND_Gate and_2, 4 bits wide
  assign out_4 = and_1_out | and_2_out;  // OR_Gate or_1, 4 bits wide
endmodule

module extensorde4bits (
  input  in_1,
  output [3:0] out_2
);


  assign out_2 = {4{in_1}};
endmodule

module extensorde8bits (
  input  in_1,
  output [7:0] out_2
);


  assign out_2 = {8{in_1}};
endmodule

// DIFERENÇA
module \diferença  (
  input  [3:0] A,
  input  [3:0] B,
  output [3:0] out_3
);

  wire comparador4bits_1_a___b_3;
  wire [3:0] subtrator_1_dif, subtrator_2_dif;

  comparador4bits comparador4bits_1 (.A(A), .B(B), .A___B_3(comparador4bits_1_a___b_3));  // open: A___B, A___B_2
  subtrator subtrator_1 (.A(A), .B(B), .Dif(subtrator_1_dif));
  subtrator subtrator_2 (.A(B), .B(A), .Dif(subtrator_2_dif));
  multiplexador multiplexador_1 (
    .A(subtrator_1_dif), .B(subtrator_2_dif), .S(comparador4bits_1_a___b_3), .out_4(out_3));
endmodule

// CORES
module cores (
  input  [3:0] \diferença_in ,
  output [7:0] vermelho,
  output [7:0] azul
);

  assign vermelho[7:4] = ~\diferença_in ;  // NOT_Gate not_1, 4 bits wide

  assign azul = {\diferença_in , 4'b1111};
  assign vermelho[3:0] = 4'b1111;
endmodule

// ACERTO
module acerto (
  input  [3:0] in_1,
  output out_2
);

  nor nor_1 (out_2, in_1[3], in_1[2], in_1[1], in_1[0]);
endmodule
